// Logisim project lab2_part2_3.circ as structural Verilog: 2 circuits, main circuit main
module main (
  input  u,
  input  v,
  input  s0,
  input  w,
  input  x,
  input  s1,
  output m
);

  wire mux1_m, mux2_m;

  mux2to1 mux1 (.x(u), .y(v), .s(s0), .m(mux1_m));
  mux2to1 mux2 (.x(w), .y(x), .s(s0), .m(mux2_m));
  mux2to1 mux3 (.x(mux1_m), .y(mux2_m), .s(s1), .m(m));
endmodule

module mux2to1 (
  input  x,
  input  y,
  input  s,
  output m
);

  Multiplexer #(.enable("false")) multiplexer_1 (.in0(x), .in1(y), .out(m), .sel(s));
endmodule
