// Logisim project lab3_part1_2.circ as structural Verilog: 1 circuit, main circuit main
module main (
  input  [9:0] SW,
  output LEDR0
);

  Multiplexer #(.enable("false"), .select(3)) multiplexer_1 (
    .in0(SW[0]), .in1(SW[1]), .in2(SW[2]), .in3(SW[3]), .in4(SW[4]), .in5(SW[5]), .in6(SW[6]), .in7(1'b1),
    .out(LEDR0), .sel(SW[9:7]));
endmodule
