// Logisim project lab3_part2.circ as structural Verilog: 2 circuits, main circuit main
module main (
  input  cin,
  input  [3:0] A,
  input  [3:0] B,
  output [3:0] S,
  output cout
);

  wire FA1_cout, FA2_cout, FA3_cout;

  fulladder FA1 (.cin(cin), .A(A[0]), .B(B[0]), .S(S[0]), .cout(FA1_cout));
  fulladder FA2 (.cin(FA1_cout), .A(A[1]), .B(B[1]), .S(S[1]), .cout(FA2_cout));
  fulladder FA3 (.cin(FA2_cout), .A(A[2]), .B(B[2]), .S(S[2]), .cout(FA3_cout));
  fulladder FA4 (.cin(FA3_cout), .A(A[3]), .B(B[3]), .S(S[3]), .cout(cout));
endmodule

module fulladder (
  input  cin,
  input  A,
  input  B,
  output S,
  output cout
);

  wire xor_1_out;

  xor xor_1 (xor_1_out, A, B);
  Multiplexer #(.enable("false")) multiplexer_1 (.in0(B), .in1(cin), .out(cout), .sel(xor_1_out));
  xor xor_2 (S, cin, xor_1_out);
endmodule
