// Logisim project lab4_part1&2.circ as structural Verilog: 22 circuits, main circuit main
module main (
  input  [3:0] A,
  input  Clk,
  input  [2:0] func,
  input  R,
  output [7:0] ALUout
);

  wire adder_1_cout, displayA_out0, displayA_out1, displayA_out2, displayA_out3, displayA_out4,
       displayA_out5, displayA_out6, displayB_out0, displayB_out1, displayB_out2, displayB_out3,
       displayB_out4, displayB_out5, displayB_out6, resultL_out0, resultL_out1, resultL_out2, resultL_out3,
       resultL_out4, resultL_out5, resultL_out6, resultR_out0, resultR_out1, resultR_out2, resultR_out3,
       resultR_out4, resultR_out5, resultR_out6;
  wire [7:0] adder_1_out, bit_extender_1_out, bit_extender_2_out, f0_000_s, f1_001_s, f3_011_s, f4_100_s,
       f5_101_s, f6_110_s, f7_111_s, multiplexer_1_out;

  decoder_7 displayA (
    .c3(A[3]), .c2(A[2]), .c1(A[1]), .c0(A[0]), .out0(displayA_out0), .out1(displayA_out1),
    .out2(displayA_out2), .out3(displayA_out3), .out4(displayA_out4), .out5(displayA_out5),
    .out6(displayA_out6));
  decoder_7 displayB (
    .c3(ALUout[3]), .c2(ALUout[2]), .c1(ALUout[1]), .c0(ALUout[0]), .out0(displayB_out0),
    .out1(displayB_out1), .out2(displayB_out2), .out3(displayB_out3), .out4(displayB_out4),
    .out5(displayB_out5), .out6(displayB_out6));
  _7_Segment_Display u_7_segment_display_1 (
    .g(displayA_out6), .f(displayA_out5), .a(displayA_out0), .b(displayA_out1), .e(displayA_out4),
    .d(displayA_out3), .c(displayA_out2));  // open: dp
  _7_Segment_Display u_7_segment_display_2 (
    .g(displayB_out6), .f(displayB_out5), .a(displayB_out0), .b(displayB_out1), .e(displayB_out4),
    .d(displayB_out3), .c(displayB_out2));  // open: dp
  assign bit_extender_1_out = {{4{1'b0}}, A};  // Bit_Extender bit_extender_1
  assign bit_extender_2_out = {{4{1'b0}}, ALUout[3:0]};  // Bit_Extender bit_extender_2
  Adder adder_1 (.a(bit_extender_1_out), .b(bit_extender_2_out), .out(adder_1_out), .cin(1'b0), .cout(adder_1_cout));
  f0_adder f0_000 (.input_A(A), .S(f0_000_s));
  f1_adder f1_001 (.A(A), .B(ALUout[3:0]), .S(f1_001_s));
  f3 f3_011 (.A(A), .B(ALUout[3:0]), .S(f3_011_s));
  f4 f4_100 (.A(A), .B(ALUout[3:0]), .S(f4_100_s));
  f5_leftshift f5_101 (.B(ALUout[3:0]), .A(A), .S(f5_101_s));
  f6_lrightshift f6_110 (.B(ALUout[3:0]), .A(A), .S(f6_110_s));
  f7_multiplier f7_111 (.B(ALUout[3:0]), .A(A), .S(f7_111_s));
  Multiplexer #(.enable("false"), .select(3), .width(8)) multiplexer_1 (
    .in0(f0_000_s), .in1(f1_001_s), .in2(adder_1_out), .in3(f3_011_s), .in4(f4_100_s), .in5(f5_101_s),
    .in6(f6_110_s), .in7(f7_111_s), .out(multiplexer_1_out), .sel(func));
  Register register_1 (.D(multiplexer_1_out), .en(1'b1), .clk(Clk), .Q(ALUout), .clr(R));
  Pull_Resistor pull_resistor_1 (.node(ALUout[7]));
  Pull_Resistor pull_resistor_2 (.node(ALUout[6]));
  Pull_Resistor pull_resistor_3 (.node(ALUout[5]));
  Pull_Resistor pull_resistor_4 (.node(ALUout[4]));
  LED LEDR0 (.in(ALUout[0]));
  LED LEDR1 (.in(ALUout[1]));
  LED LEDR2 (.in(ALUout[2]));
  LED LEDR3 (.in(ALUout[3]));
  LED LEDR4 (.in(ALUout[4]));
  LED LEDR5 (.in(ALUout[5]));
  LED LEDR6 (.in(ALUout[6]));
  LED LEDR7 (.in(ALUout[7]));
  decoder_7 resultL (
    .c3(ALUout[7]), .c2(ALUout[6]), .c1(ALUout[5]), .c0(ALUout[4]), .out0(resultL_out0), .out1(resultL_out1),
    .out2(resultL_out2), .out3(resultL_out3), .out4(resultL_out4), .out5(resultL_out5), .out6(resultL_out6));
  _7_Segment_Display u_7_segment_display_3 (
    .g(resultL_out6), .f(resultL_out5), .a(resultL_out0), .b(resultL_out1), .e(resultL_out4),
    .d(resultL_out3), .c(resultL_out2));  // open: dp
  decoder_7 resultR (
    .c3(ALUout[3]), .c2(ALUout[2]), .c1(ALUout[1]), .c0(ALUout[0]), .out0(resultR_out0), .out1(resultR_out1),
    .out2(resultR_out2), .out3(resultR_out3), .out4(resultR_out4), .out5(resultR_out5), .out6(resultR_out6));
  _7_Segment_Display u_7_segment_display_4 (
    .g(resultR_out6), .f(resultR_out5), .a(resultR_out0), .b(resultR_out1), .e(resultR_out4),
    .d(resultR_out3), .c(resultR_out2));  // open: dp
  // also tied to GND on the sheet: adder_1_cout
endmodule

module mux2to1 (
  input  x,
  input  y,
  input  s,
  output m
);

  Multiplexer #(.enable("false")) multiplexer_1 (.in0(x), .in1(y), .out(m), .sel(s));
endmodule

module mux4to1 (
  input  u,
  input  v,
  input  s0,
  input  w,
  input  x,
  input  s1,
  output m
);

  wire mux2to1_1_m, mux2to1_2_m;

  mux2to1 mux2to1_1 (.x(u), .y(v), .s(s0), .m(mux2to1_1_m));
  mux2to1 mux2to1_2 (.x(w), .y(x), .s(s0), .m(mux2to1_2_m));
  mux2to1 mux2to1_3 (.x(mux2to1_1_m), .y(mux2to1_2_m), .s(s1), .m(m));
endmodule

module seg0 (
  input  c3,
  input  c2,
  input  c1,
  input  c0,
  output out_seg0
);

  wire a_out, b_out, c_out, d_out, e_out, f_out, not_1_out, not_2_out, not_3_out, not_4_out;

  not not_1 (not_1_out, c3);
  not not_2 (not_2_out, c2);
  not not_3 (not_3_out, c1);
  not not_4 (not_4_out, c0);
  and a (a_out, not_4_out, c2, c3);
  and b (b_out, c2, not_1_out, c0);
  and c (c_out, c1, not_1_out);
  and d (d_out, not_2_out, not_4_out);
  and e (e_out, c1, c2);
  and f (f_out, not_3_out, c3, not_2_out);
  or g (out_seg0, a_out, b_out, c_out, d_out, e_out, f_out);
endmodule

module seg1 (
  input  c3,
  input  c2,
  input  c1,
  input  c0,
  output out_seg1
);

  wire a_out, b_out, c_out, d_out, e_out, not_1_out, not_2_out, not_3_out, not_4_out;

  not not_1 (not_1_out, c3);
  not not_2 (not_2_out, c2);
  not not_3 (not_3_out, c1);
  not not_4 (not_4_out, c0);
  and a (a_out, not_1_out, c1, c0);
  and b (b_out, not_1_out, not_2_out);
  and c (c_out, not_1_out, not_3_out, not_4_out);
  and d (d_out, c3, not_3_out, c0);
  and e (e_out, not_2_out, not_4_out);
  or f (out_seg1, a_out, b_out, c_out, d_out, e_out);
endmodule

module seg2 (
  input  c3,
  input  c2,
  input  c1,
  input  c0,
  output out_seg2
);

  wire a_out, b_out, c_out, d_out, e_out, not_1_out, not_2_out, not_3_out;

  not not_1 (not_1_out, c3);
  not not_2 (not_2_out, c2);
  not not_3 (not_3_out, c1);
  and a (a_out, c3, not_2_out);
  and b (b_out, not_1_out, c2);
  and c (c_out, not_1_out, not_3_out);
  and d (d_out, not_1_out, c0);
  and e (e_out, c0, not_3_out);
  or f (out_seg2, a_out, b_out, c_out, d_out, e_out);
endmodule

module seg3 (
  input  c3,
  input  c2,
  input  c1,
  input  c0,
  output out_seg3
);

  wire a_out, b_out, c_out, d_out, e_out, not_1_out, not_2_out, not_3_out, not_4_out;

  not not_1 (not_1_out, c3);
  not not_2 (not_2_out, c2);
  not not_3 (not_3_out, c1);
  not not_4 (not_4_out, c0);
  and a (a_out, c2, not_3_out, c0);
  and b (b_out, c3, not_3_out, not_4_out);
  and c (c_out, c0, not_2_out, c1);
  and d (d_out, not_1_out, not_2_out, not_4_out);
  and e (e_out, c1, c2, not_4_out);
  or f (out_seg3, a_out, b_out, c_out, d_out, e_out);
endmodule

module seg4 (
  input  c3,
  input  c2,
  input  c1,
  input  c0,
  output out_seg4
);

  wire a_out, b_out, c_out, d_out, not_1_out, not_2_out;

  not not_1 (not_1_out, c2);
  not not_2 (not_2_out, c0);
  and a (a_out, c3, c2);
  and b (b_out, not_1_out, not_2_out);
  and c (c_out, c1, not_2_out);
  and d (d_out, c3, c1);
  or e (out_seg4, a_out, b_out, c_out, d_out);
endmodule

module seg5 (
  input  c3,
  input  c2,
  input  c1,
  input  c0,
  output out_seg5
);

  wire a_out, b_out, c_out, d_out, e_out, not_1_out, not_2_out, not_3_out, not_4_out;

  not not_1 (not_1_out, c3);
  not not_2 (not_2_out, c2);
  not not_3 (not_3_out, c1);
  not not_4 (not_4_out, c0);
  and a (a_out, c3, not_2_out);
  and b (b_out, not_3_out, not_1_out, c2);
  and c (c_out, c3, c1);
  and d (d_out, c2, c1, not_4_out);
  and e (e_out, not_3_out, not_4_out);
  or f (out_seg5, a_out, b_out, c_out, d_out, e_out);
endmodule

module seg6 (
  input  c3,
  input  c2,
  input  c1,
  input  c0,
  output out_seg6
);

  wire a_out, b_out, c_out, d_out, e_out, not_1_out, not_2_out, not_3_out, not_4_out;

  not not_1 (not_1_out, c3);
  not not_2 (not_2_out, c2);
  not not_3 (not_3_out, c1);
  not not_4 (not_4_out, c0);
  and a (a_out, c3, c0);
  and b (b_out, c3, not_2_out);
  and c (c_out, not_1_out, c2, not_3_out);
  and d (d_out, c1, not_2_out);
  and e (e_out, c1, not_4_out);
  or f (out_seg6, a_out, b_out, c_out, d_out, e_out);
endmodule

module decoder_7 (
  input  c3,
  input  c2,
  input  c1,
  input  c0,
  output out0,
  output out1,
  output out2,
  output out3,
  output out4,
  output out5,
  output out6
);

  seg0 seg0_1 (.c3(c3), .c2(c2), .c1(c1), .c0(c0), .out_seg0(out0));
  seg1 seg1_1 (.c3(c3), .c2(c2), .c1(c1), .c0(c0), .out_seg1(out1));
  seg2 seg2_1 (.c3(c3), .c2(c2), .c1(c1), .c0(c0), .out_seg2(out2));
  seg3 seg3_1 (.c3(c3), .c2(c2), .c1(c1), .c0(c0), .out_seg3(out3));
  seg4 seg4_1 (.c3(c3), .c2(c2), .c1(c1), .c0(c0), .out_seg4(out4));
  seg5 seg5_1 (.c3(c3), .c2(c2), .c1(c1), .c0(c0), .out_seg5(out5));
  seg6 seg6_1 (.c3(c3), .c2(c2), .c1(c1), .c0(c0), .out_seg6(out6));
endmodule

module fulladder (
  input  cin,
  input  A,
  input  B,
  output S,
  output cout
);

  wire xor_1_out;

  xor xor_1 (xor_1_out, A, B);
  Multiplexer #(.enable("false")) multiplexer_1 (.in0(B), .in1(cin), .out(cout), .sel(xor_1_out));
  xor xor_2 (S, cin, xor_1_out);
endmodule

module f1_adder (
  input  [3:0] A,
  input  [3:0] B,
  output [7:0] S
);

  wire FA1_cout, FA2_cout, FA3_cout;
  wire [4:0] FA1_s;

  fulladder FA1 (.cin(1'b0), .A(A[0]), .B(B[0]), .S(FA1_s[0]), .cout(FA1_cout));
  fulladder FA2 (.cin(FA1_cout), .A(A[1]), .B(B[1]), .S(FA1_s[1]), .cout(FA2_cout));
  fulladder FA3 (.cin(FA2_cout), .A(A[2]), .B(B[2]), .S(FA1_s[2]), .cout(FA3_cout));
  fulladder FA4 (.cin(FA3_cout), .A(A[3]), .B(B[3]), .S(FA1_s[3]), .cout(FA1_s[4]));
  assign S = {{3{1'b0}}, FA1_s};  // Bit_Extender bit_extender_1
endmodule

module f0_adder (
  input  [3:0] input_A,
  output [7:0] S
);

  wire FA1_cout, FA2_cout, FA3_cout;
  wire [4:0] FA1_s;

  fulladder FA1 (.cin(1'b1), .A(input_A[0]), .B(1'b0), .S(FA1_s[0]), .cout(FA1_cout));
  fulladder FA2 (.cin(FA1_cout), .A(input_A[1]), .B(1'b0), .S(FA1_s[1]), .cout(FA2_cout));
  fulladder FA3 (.cin(FA2_cout), .A(input_A[2]), .B(1'b0), .S(FA1_s[2]), .cout(FA3_cout));
  fulladder FA4 (.cin(FA3_cout), .A(input_A[3]), .B(1'b0), .S(FA1_s[3]), .cout(FA1_s[4]));
  assign S = {{3{1'b0}}, FA1_s};  // Bit_Extender bit_extender_1
endmodule

module f3 (
  input  [3:0] A,
  input  [3:0] B,
  output [7:0] S
);

  xor g0 (S[0], A[0], B[0]);
  xor g1 (S[1], A[1], B[1]);
  xor g2 (S[2], A[2], B[2]);
  xor g3 (S[3], A[3], B[3]);
  or g4 (S[4], A[0], B[0]);
  or g5 (S[5], A[1], B[1]);
  or g6 (S[6], A[2], B[2]);
  or g7 (S[7], A[3], B[3]);
endmodule

module f4 (
  input  [3:0] A,
  input  [3:0] B,
  output [7:0] S
);

  wire or_1_out;

  or or_1 (or_1_out, A[0], A[1], A[2], A[3], B[0], B[1], B[2], B[3]);
  assign S = {{7{1'b0}}, or_1_out};  // Bit_Extender bit_extender_1
endmodule

module f5 (
  input  [3:0] B,
  input  [3:0] A,
  output [7:0] S
);


  assign S = {A, B};
endmodule

module Dlatch (
  input  D,
  input  Clk,
  output Qa,
  output Qb
);

  wire nand_1_out, nand_2_out, not_1_out;

  not not_1 (not_1_out, D);
  nand nand_1 (nand_1_out, D, Clk);
  nand nand_2 (nand_2_out, Clk, not_1_out);
  nand nand_3 (Qa, nand_1_out, Qb);
  nand nand_4 (Qb, Qa, nand_2_out);
endmodule

module master_slave_flipflop (
  input  in_1,
  input  in_2,
  output out_3,
  output out_4
);

  wire dlatch_1_qa, dlatch_1_qb, not_1_out;

  not not_1 (not_1_out, in_2);
  Dlatch dlatch_1 (.D(in_1), .Clk(in_2), .Qa(dlatch_1_qa), .Qb(dlatch_1_qb));
  Pull_Resistor pull_resistor_1 (.node(dlatch_1_qb));
  Dlatch dlatch_2 (.D(dlatch_1_qa), .Clk(not_1_out), .Qa(out_3), .Qb(out_4));
endmodule

module f5_leftshift (
  input  [3:0] B,
  input  [3:0] A,
  output [7:0] S
);

  wire [7:0] bit_extender_1_out;

  assign bit_extender_1_out = {{4{1'b0}}, B};  // Bit_Extender bit_extender_1
  Pull_Resistor pull_resistor_1 (.node(A[3]));
  Shifter shifter_1 (.in(bit_extender_1_out), .\dist (A[2:0]), .out(S));
endmodule

module f6_lrightshift (
  input  [3:0] B,
  input  [3:0] A,
  output [7:0] S
);

  wire [7:0] bit_extender_1_out;

  assign bit_extender_1_out = {{4{1'b0}}, B};  // Bit_Extender bit_extender_1
  Pull_Resistor pull_resistor_1 (.node(A[3]));
  Shifter #(.shift("lr")) shifter_1 (.in(bit_extender_1_out), .\dist (A[2:0]), .out(S));
endmodule

module f7_multiplier (
  input  [3:0] B,
  input  [3:0] A,
  output [7:0] S
);

  wire [7:0] bit_extender_1_out, bit_extender_2_out;

  assign bit_extender_1_out = {{4{1'b0}}, B};  // Bit_Extender bit_extender_1
  assign bit_extender_2_out = {{4{1'b0}}, A};  // Bit_Extender bit_extender_2
  Multiplier multiplier_1 (.a(bit_extender_1_out), .b(bit_extender_2_out), .out(S));  // open: cin, cout
endmodule
