// Logisim project lab5_part1.circ as structural Verilog: 20 circuits, main circuit main
module main (
  input  enable,
  input  clk,
  input  clear
);

  wire counter_8bit_syn_1_q0out, counter_8bit_syn_1_q1out, counter_8bit_syn_1_q2out,
       counter_8bit_syn_1_q3out, counter_8bit_syn_1_q4out, counter_8bit_syn_1_q5out,
       counter_8bit_syn_1_q6out, counter_8bit_syn_1_q7out, higher4_out0, higher4_out1, higher4_out2,
       higher4_out3, higher4_out4, higher4_out5, higher4_out6, lower4_out0, lower4_out1, lower4_out2,
       lower4_out3, lower4_out4, lower4_out5, lower4_out6;

  counter_8bit_syn counter_8bit_syn_1 (
    .enable(enable), .clk(clk), .clear_b(clear), .q0out(counter_8bit_syn_1_q0out),
    .q1out(counter_8bit_syn_1_q1out), .q2out(counter_8bit_syn_1_q2out), .q3out(counter_8bit_syn_1_q3out),
    .q4out(counter_8bit_syn_1_q4out), .q5out(counter_8bit_syn_1_q5out), .q6out(counter_8bit_syn_1_q6out),
    .q7out(counter_8bit_syn_1_q7out));
  decoder_7 lower4 (
    .c3(counter_8bit_syn_1_q3out), .c2(counter_8bit_syn_1_q2out), .c1(counter_8bit_syn_1_q1out),
    .c0(counter_8bit_syn_1_q0out), .out0(lower4_out0), .out1(lower4_out1), .out2(lower4_out2),
    .out3(lower4_out3), .out4(lower4_out4), .out5(lower4_out5), .out6(lower4_out6));
  decoder_7 higher4 (
    .c3(counter_8bit_syn_1_q7out), .c2(counter_8bit_syn_1_q6out), .c1(counter_8bit_syn_1_q5out),
    .c0(counter_8bit_syn_1_q4out), .out0(higher4_out0), .out1(higher4_out1), .out2(higher4_out2),
    .out3(higher4_out3), .out4(higher4_out4), .out5(higher4_out5), .out6(higher4_out6));
  _7_Segment_Display u_7_segment_display_1 (
    .g(lower4_out6), .f(lower4_out5), .a(lower4_out0), .b(lower4_out1), .e(lower4_out4), .d(lower4_out3),
    .c(lower4_out2));  // open: dp
  _7_Segment_Display u_7_segment_display_2 (
    .g(higher4_out6), .f(higher4_out5), .a(higher4_out0), .b(higher4_out1), .e(higher4_out4),
    .d(higher4_out3), .c(higher4_out2));  // open: dp
endmodule

module mux2to1 (
  input  x,
  input  y,
  input  s,
  output m
);

  Multiplexer #(.enable("false")) multiplexer_1 (.in0(x), .in1(y), .out(m), .sel(s));
endmodule

module mux4to1 (
  input  u,
  input  v,
  input  s0,
  input  w,
  input  x,
  input  s1,
  output m
);

  wire mux2to1_1_m, mux2to1_2_m;

  mux2to1 mux2to1_1 (.x(u), .y(v), .s(s0), .m(mux2to1_1_m));
  mux2to1 mux2to1_2 (.x(w), .y(x), .s(s0), .m(mux2to1_2_m));
  mux2to1 mux2to1_3 (.x(mux2to1_1_m), .y(mux2to1_2_m), .s(s1), .m(m));
endmodule

module seg0 (
  input  c3,
  input  c2,
  input  c1,
  input  c0,
  output out_seg0
);

  wire a_out, b_out, c_out, d_out, e_out, f_out, not_1_out, not_2_out, not_3_out, not_4_out;

  not not_1 (not_1_out, c3);
  not not_2 (not_2_out, c2);
  not not_3 (not_3_out, c1);
  not not_4 (not_4_out, c0);
  and a (a_out, not_4_out, c2, c3);
  and b (b_out, c2, not_1_out, c0);
  and c (c_out, c1, not_1_out);
  and d (d_out, not_2_out, not_4_out);
  and e (e_out, c1, c2);
  and f (f_out, not_3_out, c3, not_2_out);
  or g (out_seg0, a_out, b_out, c_out, d_out, e_out, f_out);
endmodule

module seg1 (
  input  c3,
  input  c2,
  input  c1,
  input  c0,
  output out_seg1
);

  wire a_out, b_out, c_out, d_out, e_out, not_1_out, not_2_out, not_3_out, not_4_out;

  not not_1 (not_1_out, c3);
  not not_2 (not_2_out, c2);
  not not_3 (not_3_out, c1);
  not not_4 (not_4_out, c0);
  and a (a_out, not_1_out, c1, c0);
  and b (b_out, not_1_out, not_2_out);
  and c (c_out, not_1_out, not_3_out, not_4_out);
  and d (d_out, c3, not_3_out, c0);
  and e (e_out, not_2_out, not_4_out);
  or f (out_seg1, a_out, b_out, c_out, d_out, e_out);
endmodule

module seg2 (
  input  c3,
  input  c2,
  input  c1,
  input  c0,
  output out_seg2
);

  wire a_out, b_out, c_out, d_out, e_out, not_1_out, not_2_out, not_3_out;

  not not_1 (not_1_out, c3);
  not not_2 (not_2_out, c2);
  not not_3 (not_3_out, c1);
  and a (a_out, c3, not_2_out);
  and b (b_out, not_1_out, c2);
  and c (c_out, not_1_out, not_3_out);
  and d (d_out, not_1_out, c0);
  and e (e_out, c0, not_3_out);
  or f (out_seg2, a_out, b_out, c_out, d_out, e_out);
endmodule

module seg3 (
  input  c3,
  input  c2,
  input  c1,
  input  c0,
  output out_seg3
);

  wire a_out, b_out, c_out, d_out, e_out, not_1_out, not_2_out, not_3_out, not_4_out;

  not not_1 (not_1_out, c3);
  not not_2 (not_2_out, c2);
  not not_3 (not_3_out, c1);
  not not_4 (not_4_out, c0);
  and a (a_out, c2, not_3_out, c0);
  and b (b_out, c3, not_3_out, not_4_out);
  and c (c_out, c0, not_2_out, c1);
  and d (d_out, not_1_out, not_2_out, not_4_out);
  and e (e_out, c1, c2, not_4_out);
  or f (out_seg3, a_out, b_out, c_out, d_out, e_out);
endmodule

module seg4 (
  input  c3,
  input  c2,
  input  c1,
  input  c0,
  output out_seg4
);

  wire a_out, b_out, c_out, d_out, not_1_out, not_2_out;

  not not_1 (not_1_out, c2);
  not not_2 (not_2_out, c0);
  and a (a_out, c3, c2);
  and b (b_out, not_1_out, not_2_out);
  and c (c_out, c1, not_2_out);
  and d (d_out, c3, c1);
  or e (out_seg4, a_out, b_out, c_out, d_out);
endmodule

module seg5 (
  input  c3,
  input  c2,
  input  c1,
  input  c0,
  output out_seg5
);

  wire a_out, b_out, c_out, d_out, e_out, not_1_out, not_2_out, not_3_out, not_4_out;

  not not_1 (not_1_out, c3);
  not not_2 (not_2_out, c2);
  not not_3 (not_3_out, c1);
  not not_4 (not_4_out, c0);
  and a (a_out, c3, not_2_out);
  and b (b_out, not_3_out, not_1_out, c2);
  and c (c_out, c3, c1);
  and d (d_out, c2, c1, not_4_out);
  and e (e_out, not_3_out, not_4_out);
  or f (out_seg5, a_out, b_out, c_out, d_out, e_out);
endmodule

module seg6 (
  input  c3,
  input  c2,
  input  c1,
  input  c0,
  output out_seg6
);

  wire a_out, b_out, c_out, d_out, e_out, not_1_out, not_2_out, not_3_out, not_4_out;

  not not_1 (not_1_out, c3);
  not not_2 (not_2_out, c2);
  not not_3 (not_3_out, c1);
  not not_4 (not_4_out, c0);
  and a (a_out, c3, c0);
  and b (b_out, c3, not_2_out);
  and c (c_out, not_1_out, c2, not_3_out);
  and d (d_out, c1, not_2_out);
  and e (e_out, c1, not_4_out);
  or f (out_seg6, a_out, b_out, c_out, d_out, e_out);
endmodule

module decoder_7 (
  input  c3,
  input  c2,
  input  c1,
  input  c0,
  output out0,
  output out1,
  output out2,
  output out3,
  output out4,
  output out5,
  output out6
);

  seg0 seg0_1 (.c3(c3), .c2(c2), .c1(c1), .c0(c0), .out_seg0(out0));
  seg1 seg1_1 (.c3(c3), .c2(c2), .c1(c1), .c0(c0), .out_seg1(out1));
  seg2 seg2_1 (.c3(c3), .c2(c2), .c1(c1), .c0(c0), .out_seg2(out2));
  seg3 seg3_1 (.c3(c3), .c2(c2), .c1(c1), .c0(c0), .out_seg3(out3));
  seg4 seg4_1 (.c3(c3), .c2(c2), .c1(c1), .c0(c0), .out_seg4(out4));
  seg5 seg5_1 (.c3(c3), .c2(c2), .c1(c1), .c0(c0), .out_seg5(out5));
  seg6 seg6_1 (.c3(c3), .c2(c2), .c1(c1), .c0(c0), .out_seg6(out6));
endmodule

module fulladder (
  input  cin,
  input  A,
  input  B,
  output S,
  output cout
);

  wire xor_1_out;

  xor xor_1 (xor_1_out, A, B);
  Multiplexer #(.enable("false")) multiplexer_1 (.in0(B), .in1(cin), .out(cout), .sel(xor_1_out));
  xor xor_2 (S, cin, xor_1_out);
endmodule

module Dlatch (
  input  D,
  input  Clk,
  output Qa,
  output Qb
);

  wire nand_1_out, nand_2_out, not_1_out;

  not not_1 (not_1_out, D);
  nand nand_1 (nand_1_out, D, Clk);
  nand nand_2 (nand_2_out, Clk, not_1_out);
  nand nand_3 (Qa, nand_1_out, Qb);
  nand nand_4 (Qb, Qa, nand_2_out);
endmodule

module master_slave_flipflop (
  input  in_1,
  input  in_2,
  output out_3,
  output out_4
);

  wire dlatch_1_qa, dlatch_1_qb, not_1_out;

  not not_1 (not_1_out, in_2);
  Dlatch dlatch_1 (.D(in_1), .Clk(in_2), .Qa(dlatch_1_qa), .Qb(dlatch_1_qb));
  Pull_Resistor pull_resistor_1 (.node(dlatch_1_qb));
  Dlatch dlatch_2 (.D(dlatch_1_qa), .Clk(not_1_out), .Qa(out_3), .Qb(out_4));
endmodule

module f5_leftshift (
  input  [3:0] B,
  input  [3:0] A,
  output [7:0] S
);

  wire [7:0] bit_extender_1_out;

  assign bit_extender_1_out = {{4{1'b0}}, B};  // Bit_Extender bit_extender_1
  Pull_Resistor pull_resistor_1 (.node(A[3]));
  Shifter shifter_1 (.in(bit_extender_1_out), .\dist (A[2:0]), .out(S));
endmodule

module f6_lrightshift (
  input  [3:0] B,
  input  [3:0] A,
  output [7:0] S
);

  wire [7:0] bit_extender_1_out;

  assign bit_extender_1_out = {{4{1'b0}}, B};  // Bit_Extender bit_extender_1
  Pull_Resistor pull_resistor_1 (.node(A[3]));
  Shifter #(.shift("lr")) shifter_1 (.in(bit_extender_1_out), .\dist (A[2:0]), .out(S));
endmodule

module f7_multiplier (
  input  [3:0] B,
  input  [3:0] A,
  output [7:0] S
);

  wire [7:0] bit_extender_1_out, bit_extender_2_out;

  assign bit_extender_1_out = {{4{1'b0}}, B};  // Bit_Extender bit_extender_1
  assign bit_extender_2_out = {{4{1'b0}}, A};  // Bit_Extender bit_extender_2
  Multiplier multiplier_1 (.a(bit_extender_1_out), .b(bit_extender_2_out), .out(S));  // open: cin, cout
endmodule

module shift_register_1bit (
  input  load_val,
  input  inp,
  input  shift,
  input  load_n,
  input  clk,
  input  reset,
  output outp
);

  wire multiplexer_1_out, multiplexer_2_out;

  Multiplexer #(.enable("false")) multiplexer_1 (.in0(outp), .in1(inp), .out(multiplexer_1_out), .sel(shift));
  Multiplexer #(.enable("false")) multiplexer_2 (
    .in0(load_val), .in1(multiplexer_1_out), .out(multiplexer_2_out), .sel(load_n));
  D_Flip_Flop d_ff_1 (.D(multiplexer_2_out), .clk(clk), .Q(outp), .reset(reset));  // open: Qn, preset
endmodule

module shift_register_8bits (
  input  [7:0] load_val,
  input  ShiftRight,
  input  load_n,
  input  Clk,
  input  reset,
  input  ASR,
  output [7:0] Q
);

  wire multiplexer_1_out;

  Multiplexer #(.enable("false")) multiplexer_1 (.in0(1'b0), .in1(Q[7]), .out(multiplexer_1_out), .sel(ASR));
  shift_register_1bit Q7 (
    .load_val(load_val[7]), .inp(multiplexer_1_out), .shift(ShiftRight), .load_n(load_n), .clk(Clk),
    .reset(reset), .outp(Q[7]));
  shift_register_1bit Q6 (
    .load_val(load_val[6]), .inp(Q[7]), .shift(ShiftRight), .load_n(load_n), .clk(Clk), .reset(reset),
    .outp(Q[6]));
  shift_register_1bit Q5 (
    .load_val(load_val[5]), .inp(Q[6]), .shift(ShiftRight), .load_n(load_n), .clk(Clk), .reset(reset),
    .outp(Q[5]));
  shift_register_1bit Q4 (
    .load_val(load_val[4]), .inp(Q[5]), .shift(ShiftRight), .load_n(load_n), .clk(Clk), .reset(reset),
    .outp(Q[4]));
  shift_register_1bit Q3 (
    .load_val(load_val[3]), .inp(Q[4]), .shift(ShiftRight), .load_n(load_n), .clk(Clk), .reset(reset),
    .outp(Q[3]));
  shift_register_1bit Q2 (
    .load_val(load_val[2]), .inp(Q[3]), .shift(ShiftRight), .load_n(load_n), .clk(Clk), .reset(reset),
    .outp(Q[2]));
  shift_register_1bit Q1 (
    .load_val(load_val[1]), .inp(Q[2]), .shift(ShiftRight), .load_n(load_n), .clk(Clk), .reset(reset),
    .outp(Q[1]));
  shift_register_1bit Q0 (
    .load_val(load_val[0]), .inp(Q[1]), .shift(ShiftRight), .load_n(load_n), .clk(Clk), .reset(reset),
    .outp(Q[0]));
endmodule

module counter_8bit_syn (
  input  enable,
  input  clk,
  input  clear_b,
  output q0out,
  output q1out,
  output q2out,
  output q3out,
  output q4out,
  output q5out,
  output q6out,
  output q7out
);

  wire and_1_out, and_2_out, and_3_out, and_4_out, and_5_out, and_6_out, and_7_out;

  T_Flip_Flop Q0 (.T(enable), .clk(clk), .Q(q0out), .reset(clear_b));  // open: Qn, preset
  and and_1 (and_1_out, enable, q0out);
  T_Flip_Flop Q1 (.T(and_1_out), .clk(clk), .Q(q1out), .reset(clear_b));  // open: Qn, preset
  and and_2 (and_2_out, and_1_out, q1out);
  T_Flip_Flop Q2 (.T(and_2_out), .clk(clk), .Q(q2out), .reset(clear_b));  // open: Qn, preset
  and and_3 (and_3_out, and_2_out, q2out);
  T_Flip_Flop Q3 (.T(and_3_out), .clk(clk), .Q(q3out), .reset(clear_b));  // open: Qn, preset
  and and_4 (and_4_out, and_3_out, q3out);
  T_Flip_Flop Q4 (.T(and_4_out), .clk(clk), .Q(q4out), .reset(clear_b));  // open: Qn, preset
  and and_5 (and_5_out, and_4_out, q4out);
  T_Flip_Flop Q5 (.T(and_5_out), .clk(clk), .Q(q5out), .reset(clear_b));  // open: Qn, preset
  and and_6 (and_6_out, and_5_out, q5out);
  T_Flip_Flop Q6 (.T(and_6_out), .clk(clk), .Q(q6out), .reset(clear_b));  // open: Qn, preset
  and and_7 (and_7_out, and_6_out, q6out);
  T_Flip_Flop Q7 (.T(and_7_out), .clk(clk), .Q(q7out), .reset(clear_b));  // open: Qn, preset
endmodule
