// Logisim project lab5_part3.circ as structural Verilog: 28 circuits, main circuit main
module main (
  input  SW0,
  input  SW1,
  input  SW2
);

  wire KEY0_out, KEY1_out, morse_code_1_led_out;

  Button KEY0 (.out(KEY0_out));
  Button KEY1 (.out(KEY1_out));
  LED LEDR0 (.in(morse_code_1_led_out));
  morse_code morse_code_1 (
    .reset(KEY0_out), .load(KEY1_out), .s0(SW0), .s1(SW1), .s2(SW2), .LED_out(morse_code_1_led_out));
endmodule

module mux2to1 (
  input  x,
  input  y,
  input  s,
  output m
);

  Multiplexer #(.enable("false")) multiplexer_1 (.in0(x), .in1(y), .out(m), .sel(s));
endmodule

module mux4to1 (
  input  u,
  input  v,
  input  s0,
  input  w,
  input  x,
  input  s1,
  output m
);

  wire mux2to1_1_m, mux2to1_2_m;

  mux2to1 mux2to1_1 (.x(u), .y(v), .s(s0), .m(mux2to1_1_m));
  mux2to1 mux2to1_2 (.x(w), .y(x), .s(s0), .m(mux2to1_2_m));
  mux2to1 mux2to1_3 (.x(mux2to1_1_m), .y(mux2to1_2_m), .s(s1), .m(m));
endmodule

module seg0 (
  input  c3,
  input  c2,
  input  c1,
  input  c0,
  output out_seg0
);

  wire a_out, b_out, c_out, d_out, e_out, f_out, not_1_out, not_2_out, not_3_out, not_4_out;

  not not_1 (not_1_out, c3);
  not not_2 (not_2_out, c2);
  not not_3 (not_3_out, c1);
  not not_4 (not_4_out, c0);
  and a (a_out, not_4_out, c2, c3);
  and b (b_out, c2, not_1_out, c0);
  and c (c_out, c1, not_1_out);
  and d (d_out, not_2_out, not_4_out);
  and e (e_out, c1, c2);
  and f (f_out, not_3_out, c3, not_2_out);
  or g (out_seg0, a_out, b_out, c_out, d_out, e_out, f_out);
endmodule

module seg1 (
  input  c3,
  input  c2,
  input  c1,
  input  c0,
  output out_seg1
);

  wire a_out, b_out, c_out, d_out, e_out, not_1_out, not_2_out, not_3_out, not_4_out;

  not not_1 (not_1_out, c3);
  not not_2 (not_2_out, c2);
  not not_3 (not_3_out, c1);
  not not_4 (not_4_out, c0);
  and a (a_out, not_1_out, c1, c0);
  and b (b_out, not_1_out, not_2_out);
  and c (c_out, not_1_out, not_3_out, not_4_out);
  and d (d_out, c3, not_3_out, c0);
  and e (e_out, not_2_out, not_4_out);
  or f (out_seg1, a_out, b_out, c_out, d_out, e_out);
endmodule

module seg2 (
  input  c3,
  input  c2,
  input  c1,
  input  c0,
  output out_seg2
);

  wire a_out, b_out, c_out, d_out, e_out, not_1_out, not_2_out, not_3_out;

  not not_1 (not_1_out, c3);
  not not_2 (not_2_out, c2);
  not not_3 (not_3_out, c1);
  and a (a_out, c3, not_2_out);
  and b (b_out, not_1_out, c2);
  and c (c_out, not_1_out, not_3_out);
  and d (d_out, not_1_out, c0);
  and e (e_out, c0, not_3_out);
  or f (out_seg2, a_out, b_out, c_out, d_out, e_out);
endmodule

module seg3 (
  input  c3,
  input  c2,
  input  c1,
  input  c0,
  output out_seg3
);

  wire a_out, b_out, c_out, d_out, e_out, not_1_out, not_2_out, not_3_out, not_4_out;

  not not_1 (not_1_out, c3);
  not not_2 (not_2_out, c2);
  not not_3 (not_3_out, c1);
  not not_4 (not_4_out, c0);
  and a (a_out, c2, not_3_out, c0);
  and b (b_out, c3, not_3_out, not_4_out);
  and c (c_out, c0, not_2_out, c1);
  and d (d_out, not_1_out, not_2_out, not_4_out);
  and e (e_out, c1, c2, not_4_out);
  or f (out_seg3, a_out, b_out, c_out, d_out, e_out);
endmodule

module seg4 (
  input  c3,
  input  c2,
  input  c1,
  input  c0,
  output out_seg4
);

  wire a_out, b_out, c_out, d_out, not_1_out, not_2_out;

  not not_1 (not_1_out, c2);
  not not_2 (not_2_out, c0);
  and a (a_out, c3, c2);
  and b (b_out, not_1_out, not_2_out);
  and c (c_out, c1, not_2_out);
  and d (d_out, c3, c1);
  or e (out_seg4, a_out, b_out, c_out, d_out);
endmodule

module seg5 (
  input  c3,
  input  c2,
  input  c1,
  input  c0,
  output out_seg5
);

  wire a_out, b_out, c_out, d_out, e_out, not_1_out, not_2_out, not_3_out, not_4_out;

  not not_1 (not_1_out, c3);
  not not_2 (not_2_out, c2);
  not not_3 (not_3_out, c1);
  not not_4 (not_4_out, c0);
  and a (a_out, c3, not_2_out);
  and b (b_out, not_3_out, not_1_out, c2);
  and c (c_out, c3, c1);
  and d (d_out, c2, c1, not_4_out);
  and e (e_out, not_3_out, not_4_out);
  or f (out_seg5, a_out, b_out, c_out, d_out, e_out);
endmodule

module seg6 (
  input  c3,
  input  c2,
  input  c1,
  input  c0,
  output out_seg6
);

  wire a_out, b_out, c_out, d_out, e_out, not_1_out, not_2_out, not_3_out, not_4_out;

  not not_1 (not_1_out, c3);
  not not_2 (not_2_out, c2);
  not not_3 (not_3_out, c1);
  not not_4 (not_4_out, c0);
  and a (a_out, c3, c0);
  and b (b_out, c3, not_2_out);
  and c (c_out, not_1_out, c2, not_3_out);
  and d (d_out, c1, not_2_out);
  and e (e_out, c1, not_4_out);
  or f (out_seg6, a_out, b_out, c_out, d_out, e_out);
endmodule

module decoder_7 (
  input  c3,
  input  c2,
  input  c1,
  input  c0,
  output out0,
  output out1,
  output out2,
  output out3,
  output out4,
  output out5,
  output out6
);

  seg0 seg0_1 (.c3(c3), .c2(c2), .c1(c1), .c0(c0), .out_seg0(out0));
  seg1 seg1_1 (.c3(c3), .c2(c2), .c1(c1), .c0(c0), .out_seg1(out1));
  seg2 seg2_1 (.c3(c3), .c2(c2), .c1(c1), .c0(c0), .out_seg2(out2));
  seg3 seg3_1 (.c3(c3), .c2(c2), .c1(c1), .c0(c0), .out_seg3(out3));
  seg4 seg4_1 (.c3(c3), .c2(c2), .c1(c1), .c0(c0), .out_seg4(out4));
  seg5 seg5_1 (.c3(c3), .c2(c2), .c1(c1), .c0(c0), .out_seg5(out5));
  seg6 seg6_1 (.c3(c3), .c2(c2), .c1(c1), .c0(c0), .out_seg6(out6));
endmodule

module fulladder (
  input  cin,
  input  A,
  input  B,
  output S,
  output cout
);

  wire xor_1_out;

  xor xor_1 (xor_1_out, A, B);
  Multiplexer #(.enable("false")) multiplexer_1 (.in0(B), .in1(cin), .out(cout), .sel(xor_1_out));
  xor xor_2 (S, cin, xor_1_out);
endmodule

module Dlatch (
  input  D,
  input  Clk,
  output Qa,
  output Qb
);

  wire nand_1_out, nand_2_out, not_1_out;

  not not_1 (not_1_out, D);
  nand nand_1 (nand_1_out, D, Clk);
  nand nand_2 (nand_2_out, Clk, not_1_out);
  nand nand_3 (Qa, nand_1_out, Qb);
  nand nand_4 (Qb, Qa, nand_2_out);
endmodule

module master_slave_flipflop (
  input  in_1,
  input  in_2,
  output out_3,
  output out_4
);

  wire dlatch_1_qa, dlatch_1_qb, not_1_out;

  not not_1 (not_1_out, in_2);
  Dlatch dlatch_1 (.D(in_1), .Clk(in_2), .Qa(dlatch_1_qa), .Qb(dlatch_1_qb));
  Pull_Resistor pull_resistor_1 (.node(dlatch_1_qb));
  Dlatch dlatch_2 (.D(dlatch_1_qa), .Clk(not_1_out), .Qa(out_3), .Qb(out_4));
endmodule

module f5_leftshift (
  input  [3:0] B,
  input  [3:0] A,
  output [7:0] S
);

  wire [7:0] bit_extender_1_out;

  assign bit_extender_1_out = {{4{1'b0}}, B};  // Bit_Extender bit_extender_1
  Pull_Resistor pull_resistor_1 (.node(A[3]));
  Shifter shifter_1 (.in(bit_extender_1_out), .\dist (A[2:0]), .out(S));
endmodule

module f6_lrightshift (
  input  [3:0] B,
  input  [3:0] A,
  output [7:0] S
);

  wire [7:0] bit_extender_1_out;

  assign bit_extender_1_out = {{4{1'b0}}, B};  // Bit_Extender bit_extender_1
  Pull_Resistor pull_resistor_1 (.node(A[3]));
  Shifter #(.shift("lr")) shifter_1 (.in(bit_extender_1_out), .\dist (A[2:0]), .out(S));
endmodule

module f7_multiplier (
  input  [3:0] B,
  input  [3:0] A,
  output [7:0] S
);

  wire [7:0] bit_extender_1_out, bit_extender_2_out;

  assign bit_extender_1_out = {{4{1'b0}}, B};  // Bit_Extender bit_extender_1
  assign bit_extender_2_out = {{4{1'b0}}, A};  // Bit_Extender bit_extender_2
  Multiplier multiplier_1 (.a(bit_extender_1_out), .b(bit_extender_2_out), .out(S));  // open: cin, cout
endmodule

module shift_register_1bit (
  input  load_val,
  input  inp,
  input  shift,
  input  load_n,
  input  clk,
  input  reset,
  output outp
);

  wire multiplexer_1_out, multiplexer_2_out;

  Multiplexer #(.enable("false")) multiplexer_1 (.in0(outp), .in1(inp), .out(multiplexer_1_out), .sel(shift));
  Multiplexer #(.enable("false")) multiplexer_2 (
    .in0(load_val), .in1(multiplexer_1_out), .out(multiplexer_2_out), .sel(load_n));
  D_Flip_Flop d_ff_1 (.D(multiplexer_2_out), .clk(clk), .Q(outp), .reset(reset));  // open: Qn, preset
endmodule

module shift_register_8bits (
  input  [7:0] load_val,
  input  ShiftRight,
  input  load_n,
  input  Clk,
  input  reset,
  input  ASR,
  output [7:0] Q
);

  wire multiplexer_1_out;

  Multiplexer #(.enable("false")) multiplexer_1 (.in0(1'b0), .in1(Q[7]), .out(multiplexer_1_out), .sel(ASR));
  shift_register_1bit Q7 (
    .load_val(load_val[7]), .inp(multiplexer_1_out), .shift(ShiftRight), .load_n(load_n), .clk(Clk),
    .reset(reset), .outp(Q[7]));
  shift_register_1bit Q6 (
    .load_val(load_val[6]), .inp(Q[7]), .shift(ShiftRight), .load_n(load_n), .clk(Clk), .reset(reset),
    .outp(Q[6]));
  shift_register_1bit Q5 (
    .load_val(load_val[5]), .inp(Q[6]), .shift(ShiftRight), .load_n(load_n), .clk(Clk), .reset(reset),
    .outp(Q[5]));
  shift_register_1bit Q4 (
    .load_val(load_val[4]), .inp(Q[5]), .shift(ShiftRight), .load_n(load_n), .clk(Clk), .reset(reset),
    .outp(Q[4]));
  shift_register_1bit Q3 (
    .load_val(load_val[3]), .inp(Q[4]), .shift(ShiftRight), .load_n(load_n), .clk(Clk), .reset(reset),
    .outp(Q[3]));
  shift_register_1bit Q2 (
    .load_val(load_val[2]), .inp(Q[3]), .shift(ShiftRight), .load_n(load_n), .clk(Clk), .reset(reset),
    .outp(Q[2]));
  shift_register_1bit Q1 (
    .load_val(load_val[1]), .inp(Q[2]), .shift(ShiftRight), .load_n(load_n), .clk(Clk), .reset(reset),
    .outp(Q[1]));
  shift_register_1bit Q0 (
    .load_val(load_val[0]), .inp(Q[1]), .shift(ShiftRight), .load_n(load_n), .clk(Clk), .reset(reset),
    .outp(Q[0]));
endmodule

module counter_8bit_syn (
  input  enable,
  input  clk,
  input  clear_b,
  output q0out,
  output q1out,
  output q2out,
  output q3out,
  output q4out,
  output q5out,
  output q6out,
  output q7out
);

  wire and_1_out, and_2_out, and_3_out, and_4_out, and_5_out, and_6_out, and_7_out;

  T_Flip_Flop Q0 (.T(enable), .clk(clk), .Q(q0out), .reset(clear_b));  // open: Qn, preset
  and and_1 (and_1_out, enable, q0out);
  T_Flip_Flop Q1 (.T(and_1_out), .clk(clk), .Q(q1out), .reset(clear_b));  // open: Qn, preset
  and and_2 (and_2_out, and_1_out, q1out);
  T_Flip_Flop Q2 (.T(and_2_out), .clk(clk), .Q(q2out), .reset(clear_b));  // open: Qn, preset
  and and_3 (and_3_out, and_2_out, q2out);
  T_Flip_Flop Q3 (.T(and_3_out), .clk(clk), .Q(q3out), .reset(clear_b));  // open: Qn, preset
  and and_4 (and_4_out, and_3_out, q3out);
  T_Flip_Flop Q4 (.T(and_4_out), .clk(clk), .Q(q4out), .reset(clear_b));  // open: Qn, preset
  and and_5 (and_5_out, and_4_out, q4out);
  T_Flip_Flop Q5 (.T(and_5_out), .clk(clk), .Q(q5out), .reset(clear_b));  // open: Qn, preset
  and and_6 (and_6_out, and_5_out, q5out);
  T_Flip_Flop Q6 (.T(and_6_out), .clk(clk), .Q(q6out), .reset(clear_b));  // open: Qn, preset
  and and_7 (and_7_out, and_6_out, q6out);
  T_Flip_Flop Q7 (.T(and_7_out), .clk(clk), .Q(q7out), .reset(clear_b));  // open: Qn, preset
endmodule

module counter_4bit_display (
  input  clear,
  input  enable,
  input  clk,
  output output_Q3,
  output output_Q2,
  output output_Q1,
  output output_Q0
);

  wire not_1_out;

  not not_1 (not_1_out, enable);
  Counter #(.max('hf), .width(4)) counter_1 (
    .clr(clear), .load(not_1_out), .up(1'b1), .clk(clk), .D({output_Q3, output_Q2, output_Q1, output_Q0}),
    .Q({output_Q3, output_Q2, output_Q1, output_Q0}));  // open: count, carry
endmodule

module ratedivider (
  input  clear,
  input  clk,
  input  SW0,
  input  SW1,
  output divider_out
);

  wire half_out, not_1_out, not_2_out, one_out, or_1_out, quarter_out;
  wire [6:0] counter_1_q;

  not not_1 (not_1_out, 1'b1);
  or or_1 (or_1_out, divider_out, not_1_out);
  Counter #(.max('h7f), .ongoal("continue"), .width(7)) counter_1 (
    .clr(clear), .load(or_1_out), .up(1'b1), .clk(clk), .D({7{1'b0}}), .Q(counter_1_q));  // open: count, carry
  not not_2 (not_2_out, clk);
  and quarter (quarter_out, counter_1_q[0], counter_1_q[1], counter_1_q[2], counter_1_q[3], counter_1_q[4], counter_1_q[5], counter_1_q[6]);
  and half (half_out, counter_1_q[5], counter_1_q[4], counter_1_q[3], counter_1_q[2], counter_1_q[1], counter_1_q[0]);
  and one (one_out, counter_1_q[4], counter_1_q[3], counter_1_q[2], counter_1_q[1], counter_1_q[0]);
  mux4to1 mux4to1_1 (.u(not_2_out), .v(one_out), .s0(SW0), .w(half_out), .x(quarter_out), .s1(SW1), .m(divider_out));
endmodule

module counter_4bit (
  input  clear,
  input  clk,
  input  enable,
  output counter_out
);

  wire not_1_out, or_1_out;
  wire [3:0] counter_1_q;

  not not_1 (not_1_out, enable);
  or or_1 (or_1_out, counter_out, not_1_out);
  Counter #(.max('hf), .ongoal("continue"), .width(4)) counter_1 (
    .clr(clear), .load(or_1_out), .up(1'b1), .clk(clk), .D(4'b0000), .Q(counter_1_q));  // open: count, carry
  and and_1 (counter_out, counter_1_q[0], counter_1_q[1], counter_1_q[2], counter_1_q[3]);
endmodule

module decoder_7_withdisplay (
  input  SW_3,
  input  SW_2,
  input  SW_1,
  input  SW_0
);

  wire decoder_7_1_out0, decoder_7_1_out1, decoder_7_1_out2, decoder_7_1_out3, decoder_7_1_out4,
       decoder_7_1_out5, decoder_7_1_out6;

  decoder_7 decoder_7_1 (
    .c3(SW_3), .c2(SW_2), .c1(SW_1), .c0(SW_0), .out0(decoder_7_1_out0), .out1(decoder_7_1_out1),
    .out2(decoder_7_1_out2), .out3(decoder_7_1_out3), .out4(decoder_7_1_out4), .out5(decoder_7_1_out5),
    .out6(decoder_7_1_out6));
  _7_Segment_Display u_7_segment_display_1 (
    .g(decoder_7_1_out6), .f(decoder_7_1_out5), .a(decoder_7_1_out0), .b(decoder_7_1_out1),
    .e(decoder_7_1_out4), .d(decoder_7_1_out3), .c(decoder_7_1_out2));  // open: dp
endmodule

module counter_4bit_dis (
  input  enable,
  input  clock,
  input  clear_b,
  output q0out,
  output q1out,
  output q2out,
  output q3out
);

  wire and_1_out, and_2_out, and_3_out;

  T_Flip_Flop Q0 (.T(enable), .clk(clock), .Q(q0out), .reset(clear_b));  // open: Qn, preset
  and and_1 (and_1_out, enable, q0out);
  T_Flip_Flop Q1 (.T(and_1_out), .clk(clock), .Q(q1out), .reset(clear_b));  // open: Qn, preset
  and and_2 (and_2_out, and_1_out, q1out);
  T_Flip_Flop Q2 (.T(and_2_out), .clk(clock), .Q(q2out), .reset(clear_b));  // open: Qn, preset
  and and_3 (and_3_out, and_2_out, q2out);
  T_Flip_Flop Q3 (.T(and_3_out), .clk(clock), .Q(q3out), .reset(clear_b));  // open: Qn, preset
endmodule

module LUT (
  input  s0,
  input  s1,
  input  s2,
  output [13:0] LUT_out
);

  Multiplexer #(.enable("false"), .select(3), .width(14)) multiplexer_1 (
    .in0(14'h2a00), .in1(14'h3800), .in2(14'h2b80), .in3(14'h2ae0), .in4(14'h2ee0), .in5(14'h3ab8),
    .in6(14'h3aee), .in7(14'h3ba8), .out(LUT_out), .sel({s2, s1, s0}));
endmodule

module morse_code (
  input  reset,
  input  load,
  input  s0,
  input  s1,
  input  s2,
  output LED_out
);

  wire clock_1_out, ratedivider_2hz_1_divider_out;
  wire [12:0] pull_resistor_1_node;
  wire [13:0] lut_1_lut_out;

  Clock clock_1 (.out(clock_1_out));
  ratedivider_2hz ratedivider_2hz_1 (.reset(reset), .clk(clock_1_out), .divider_out(ratedivider_2hz_1_divider_out));
  LUT lut_1 (.s0(s0), .s1(s1), .s2(s2), .LUT_out(lut_1_lut_out));
  // Shift_Register #(.length(14)) shift_register_1: pin names not known; wires that end beside it: reset, load, ratedivider_2hz_1_divider_out, clock_1_out, 1'b0
  Pull_Resistor pull_resistor_1 (.node(pull_resistor_1_node));
endmodule

module ratedivider_2hz (
  input  reset,
  input  clk,
  output divider_out
);

  wire not_1_out, or_1_out;
  wire [3:0] counter_1_q;

  not not_1 (not_1_out, 1'b1);
  or or_1 (or_1_out, divider_out, not_1_out);
  Counter #(.max('hf), .ongoal("continue"), .width(4)) counter_1 (
    .clr(reset), .load(or_1_out), .up(1'b1), .clk(clk), .D(4'b0000), .Q(counter_1_q));  // open: count, carry
  and and_1 (divider_out, counter_1_q[0], counter_1_q[1], counter_1_q[2], counter_1_q[3]);
endmodule
