// Logisim project lab7_part1.circ as structural Verilog: 10 circuits, main circuit main
module main (
  input  output_en,
  input  clk,
  input  reset,
  input  write_en
);

  wire datapath_part1_1_write, HEX_0_out0, HEX_0_out1, HEX_0_out2, HEX_0_out3, HEX_0_out4, HEX_0_out5,
       HEX_0_out6;
  wire [3:0] datapath_part1_1_data_out, myRAM_dout;
  wire [4:0] datapath_part1_1_address_out;

  datapath_part1 datapath_part1_1 (
    .reset(reset), .clk(clk), .write_en(write_en), .write(datapath_part1_1_write),
    .address_out(datapath_part1_1_address_out), .data_out(datapath_part1_1_data_out));
  RAM #(.addrWidth(5), .dataWidth(4)) myRAM (
    .addr(datapath_part1_1_address_out), .we(datapath_part1_1_write), .oe(output_en), .clk(clk),
    .din(datapath_part1_1_data_out), .dout(myRAM_dout));
  decoder_7 HEX_0 (
    .c3(myRAM_dout[3]), .c2(myRAM_dout[2]), .c1(myRAM_dout[1]), .c0(myRAM_dout[0]), .out0(HEX_0_out0),
    .out1(HEX_0_out1), .out2(HEX_0_out2), .out3(HEX_0_out3), .out4(HEX_0_out4), .out5(HEX_0_out5),
    .out6(HEX_0_out6));
  _7_Segment_Display u_7_segment_display_1 (
    .g(HEX_0_out6), .f(HEX_0_out5), .a(HEX_0_out0), .b(HEX_0_out1), .e(HEX_0_out4), .d(HEX_0_out3),
    .c(HEX_0_out2));  // open: dp
endmodule

module seg0 (
  input  c3,
  input  c2,
  input  c1,
  input  c0,
  output out_seg0
);

  wire a_out, b_out, c_out, d_out, e_out, f_out, not_1_out, not_2_out, not_3_out, not_4_out;

  not not_1 (not_1_out, c3);
  not not_2 (not_2_out, c2);
  not not_3 (not_3_out, c1);
  not not_4 (not_4_out, c0);
  and a (a_out, not_4_out, c2, c3);
  and b (b_out, c2, not_1_out, c0);
  and c (c_out, c1, not_1_out);
  and d (d_out, not_2_out, not_4_out);
  and e (e_out, c1, c2);
  and f (f_out, not_3_out, c3, not_2_out);
  or g (out_seg0, a_out, b_out, c_out, d_out, e_out, f_out);
endmodule

module seg1 (
  input  c3,
  input  c2,
  input  c1,
  input  c0,
  output out_seg1
);

  wire a_out, b_out, c_out, d_out, e_out, not_1_out, not_2_out, not_3_out, not_4_out;

  not not_1 (not_1_out, c3);
  not not_2 (not_2_out, c2);
  not not_3 (not_3_out, c1);
  not not_4 (not_4_out, c0);
  and a (a_out, not_1_out, c1, c0);
  and b (b_out, not_1_out, not_2_out);
  and c (c_out, not_1_out, not_3_out, not_4_out);
  and d (d_out, c3, not_3_out, c0);
  and e (e_out, not_2_out, not_4_out);
  or f (out_seg1, a_out, b_out, c_out, d_out, e_out);
endmodule

module seg2 (
  input  c3,
  input  c2,
  input  c1,
  input  c0,
  output out_seg2
);

  wire a_out, b_out, c_out, d_out, e_out, not_1_out, not_2_out, not_3_out;

  not not_1 (not_1_out, c3);
  not not_2 (not_2_out, c2);
  not not_3 (not_3_out, c1);
  and a (a_out, c3, not_2_out);
  and b (b_out, not_1_out, c2);
  and c (c_out, not_1_out, not_3_out);
  and d (d_out, not_1_out, c0);
  and e (e_out, c0, not_3_out);
  or f (out_seg2, a_out, b_out, c_out, d_out, e_out);
endmodule

module seg3 (
  input  c3,
  input  c2,
  input  c1,
  input  c0,
  output out_seg3
);

  wire a_out, b_out, c_out, d_out, e_out, not_1_out, not_2_out, not_3_out, not_4_out;

  not not_1 (not_1_out, c3);
  not not_2 (not_2_out, c2);
  not not_3 (not_3_out, c1);
  not not_4 (not_4_out, c0);
  and a (a_out, c2, not_3_out, c0);
  and b (b_out, c3, not_3_out, not_4_out);
  and c (c_out, c0, not_2_out, c1);
  and d (d_out, not_1_out, not_2_out, not_4_out);
  and e (e_out, c1, c2, not_4_out);
  or f (out_seg3, a_out, b_out, c_out, d_out, e_out);
endmodule

module seg4 (
  input  c3,
  input  c2,
  input  c1,
  input  c0,
  output out_seg4
);

  wire a_out, b_out, c_out, d_out, not_1_out, not_2_out;

  not not_1 (not_1_out, c2);
  not not_2 (not_2_out, c0);
  and a (a_out, c3, c2);
  and b (b_out, not_1_out, not_2_out);
  and c (c_out, c1, not_2_out);
  and d (d_out, c3, c1);
  or e (out_seg4, a_out, b_out, c_out, d_out);
endmodule

module seg5 (
  input  c3,
  input  c2,
  input  c1,
  input  c0,
  output out_seg5
);

  wire a_out, b_out, c_out, d_out, e_out, not_1_out, not_2_out, not_3_out, not_4_out;

  not not_1 (not_1_out, c3);
  not not_2 (not_2_out, c2);
  not not_3 (not_3_out, c1);
  not not_4 (not_4_out, c0);
  and a (a_out, c3, not_2_out);
  and b (b_out, not_3_out, not_1_out, c2);
  and c (c_out, c3, c1);
  and d (d_out, c2, c1, not_4_out);
  and e (e_out, not_3_out, not_4_out);
  or f (out_seg5, a_out, b_out, c_out, d_out, e_out);
endmodule

module seg6 (
  input  c3,
  input  c2,
  input  c1,
  input  c0,
  output out_seg6
);

  wire a_out, b_out, c_out, d_out, e_out, not_1_out, not_2_out, not_3_out, not_4_out;

  not not_1 (not_1_out, c3);
  not not_2 (not_2_out, c2);
  not not_3 (not_3_out, c1);
  not not_4 (not_4_out, c0);
  and a (a_out, c3, c0);
  and b (b_out, c3, not_2_out);
  and c (c_out, not_1_out, c2, not_3_out);
  and d (d_out, c1, not_2_out);
  and e (e_out, c1, not_4_out);
  or f (out_seg6, a_out, b_out, c_out, d_out, e_out);
endmodule

module decoder_7 (
  input  c3,
  input  c2,
  input  c1,
  input  c0,
  output out0,
  output out1,
  output out2,
  output out3,
  output out4,
  output out5,
  output out6
);

  seg0 seg0_1 (.c3(c3), .c2(c2), .c1(c1), .c0(c0), .out_seg0(out0));
  seg1 seg1_1 (.c3(c3), .c2(c2), .c1(c1), .c0(c0), .out_seg1(out1));
  seg2 seg2_1 (.c3(c3), .c2(c2), .c1(c1), .c0(c0), .out_seg2(out2));
  seg3 seg3_1 (.c3(c3), .c2(c2), .c1(c1), .c0(c0), .out_seg3(out3));
  seg4 seg4_1 (.c3(c3), .c2(c2), .c1(c1), .c0(c0), .out_seg4(out4));
  seg5 seg5_1 (.c3(c3), .c2(c2), .c1(c1), .c0(c0), .out_seg5(out5));
  seg6 seg6_1 (.c3(c3), .c2(c2), .c1(c1), .c0(c0), .out_seg6(out6));
endmodule

module datapath_part1 (
  input  reset,
  input  clk,
  input  write_en,
  output write,
  output [4:0] address_out,
  output [3:0] data_out
);

  wire not_1_out;

  not not_1 (not_1_out, write_en);
  Counter #(.max('h1f), .width(5)) address_counter (
    .clr(reset), .load(not_1_out), .up(1'b1), .clk(clk), .D(address_out), .Q(address_out));  // open: count, carry
  Counter #(.max('hf), .width(4)) data_counter (
    .clr(reset), .load(not_1_out), .up(1'b1), .clk(clk), .D(data_out), .Q(data_out));  // open: count, carry

  assign write = write_en;
endmodule
