// Logisim project lab7_part2.circ as structural Verilog: 2 circuits, main circuit main
module main (
  input  enable,
  input  reset,
  input  [6:0] in_3,
  input  [6:0] in_4
);

  wire clock_1_out, datapath_1_write, not_1_out;
  wire [6:0] datapath_1_x_out, datapath_1_y_out;
  wire [7:0] counter_1_q;
  wire [23:0] datapath_1_blue;

  Clock clock_1 (.out(clock_1_out));
  Counter #(.ongoal("stay")) counter_1 (
    .clr(reset), .load(not_1_out), .up(1'b1), .clk(clock_1_out), .D({8{1'b0}}), .Q(counter_1_q));  // open: count, carry
  not not_1 (not_1_out, enable);
  datapath datapath_1 (
    .FSM_signal(counter_1_q), .X(in_3), .Y(in_4), .clk(clock_1_out), .enable(enable),
    .X_out(datapath_1_x_out), .Y_out(datapath_1_y_out), .write(datapath_1_write),
    .blue(datapath_1_blue[7:0]), .green(datapath_1_blue[15:8]), .red(datapath_1_blue[23:16]));
  // RGB_Video #(.cursor("No Cursor")) rgb_video_1: pin names not known; wires that end beside it: reset, clock_1_out, datapath_1_write, datapath_1_x_out, datapath_1_y_out, datapath_1_blue
endmodule

module datapath (
  input  [7:0] FSM_signal,
  input  [6:0] X,
  input  [6:0] Y,
  input  clk,
  input  enable,
  output [6:0] X_out,
  output [6:0] Y_out,
  output write,
  output [7:0] blue,
  output [7:0] green,
  output [7:0] red
);

  wire and_1_out, not_1_out;
  wire [6:0] bit_extender_1_out, bit_extender_2_out;
  wire [7:0] register_1_q;

  Register register_1 (.D(FSM_signal), .en(1'b1), .clk(clk), .Q(register_1_q));  // open: clr
  assign bit_extender_1_out = {{3{1'b0}}, FSM_signal[3:0]};  // Bit_Extender bit_extender_1
  assign bit_extender_2_out = {{3{1'b0}}, FSM_signal[7:4]};  // Bit_Extender bit_extender_2
  and and_1 (and_1_out, register_1_q[0], register_1_q[1], register_1_q[2], register_1_q[3], register_1_q[4], register_1_q[5], register_1_q[6], register_1_q[7]);
  Adder #(.width(7)) adder_1 (.a(X), .b(bit_extender_1_out), .out(X_out));  // open: cin, cout
  Adder #(.width(7)) adder_2 (.a(bit_extender_2_out), .b(Y), .out(Y_out));  // open: cin, cout
  not not_1 (not_1_out, and_1_out);
  and and_2 (write, not_1_out, enable);

  assign blue = {8{1'b1}};
  assign green = {8{1'b0}};
  assign red = {8{1'b1}};
endmodule
